# Fritzing sketch Smart-mailbox (saved by Fritzing 0.9.3b)
breadboards: 1

parts:
  U1 = NodeMCU V3.0
  Squix1 = OLED 0.96" 128x64 I2C SSD1306
  DHT1 = DHT22 Humidity and Temperature Sensor
  KY-1 = Keyes Photo Resistor Sensor [package=THT]
  LED2 = DUO LED RG [package="5 mm [THT]"]
  U2 = mystery part, 3 pins [chip_label=?]
  U3 = mystery part, 3 pins [chip_label=?]  # not connected
  U4 = mystery part, 3 pins [chip_label=?]  # not connected
  U5 = mystery part, 3 pins [chip_label=?]  # not connected
  U6 = mystery part, 3 pins [chip_label=?]

nets:
  N1: U1.D1, U6.pin3
  N2: U1.D2, U2.pin3
  N3: U1.D3, Squix1.SCL
  N4: U1.D4, Squix1.SCA
  3V3: U1.3V3, Squix1.VCC, DHT1.VDD, KY-1.power, U2.pin1, U6.pin1
  N5: U1.GND#6, U1.GND#13, U1.GND#16, U1.GND#33, Squix1.GND, KY-1.ground, LED2.red_anode, U2.pin2, U6.pin2
  N6: U1.D5, DHT1.DATA
  N7: U1.D6, LED2.green_anode
  N8: U1.GND#41, DHT1.GND
  N9: U1.A0, KY-1.signal

notes:
  Sessor Temperatura
  Pantalla LCD
  Led
  Fotoresistor
  Sensores Efecto Hall

custom parts:
  NodeMCU V3.0: ESP8266 based NodeMCU
  Keyes Photo Resistor Sensor: Keyes Photo Resistor Sensor Module for Arduino.
